# Fritzing sketch food_dispensor_fritzing (saved by Fritzing 1.0.7)
breadboards: 1

parts:
  L298N1 = L298N DC motor driver
  M1 = DC Motor [voltage_(max)=6V voltage_(min)=3V]
  Part1 = Arduino Uno (Rev3)
  M2 = IR break beam 3mm tx [package=THT]
  M3 = IR break beam 3mm rx [package=THT]
  JACK1 = 2.1mm Barrel Jack with Terminal Block
  J1 = Basic Servo

nets:
  N1: L298N1.OUT3, M1.pin_2
  N2: L298N1.OUT4, M1.pin_1
  N3: L298N1.12V, JACK1.POS
  GND: L298N1.GND, Part1.GND, M2.pin2, M3.pin3, JACK1.NEG, J1.gnd
  5V: L298N1.5V, Part1.5V, M2.pin1, M3.pin1, J1.vcc
  N4: L298N1.ENB, Part1.D10_PWM/SS
  N5: L298N1.IN3, Part1.D4
  N6: L298N1.IN4, Part1.D3_PWM
  N7: Part1.D9_PWM, J1.pulse
  N8: Part1.D2, M3.pin2

notes:
  Power
  Flywheel Motor
  L298N Motor Driver Board
  IR TX Sensor
  IR RX Sensor
  Dispensing Servo
  Arduino Uno

custom parts:
  L298N DC motor driver: 2x DC motor driver with 78M05 positive voltage regulator (7..35 V) L298N: max 46 V, 2 A Set 5 V Enable jumper to enable 5 V regultor (needed for the L298N) and +5 V output at screw terminal or supply external +5 V at screw terminal Set ENA and/or ENB to +5 V to enable motor permanently or supply ENA and/or ENB with PWM signal IN1 and IN2 set rotation directory for motor A (OUT1/OUT2) IN2 and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
  IR break beam 3mm tx: Infrared break beam Sensor tx module.
  IR break beam 3mm rx: Infrared break beam Sensor rx module.
